// Logisim project test1.circ as structural Verilog: 1 circuit, main circuit main
module main (
  input  w,
  input  x,
  input  y,
  input  z,
  input  x2,
  input  y2,
  input  z2
);

  wire and_1_out, and_2_out, and_3_out, not_1_out, not_2_out, or_1_out, or_2_out, or_3_out;

  not not_1 (not_1_out, w);
  not not_2 (not_2_out, z2);
  and and_1 (and_1_out, not_1_out, y);
  or or_1 (or_1_out, x, y);
  and and_2 (and_2_out, x2, y2);
  and and_3 (and_3_out, or_1_out, z);
  or or_2 (or_2_out, and_2_out, not_2_out);
  or or_3 (or_3_out, and_1_out, and_3_out);
endmodule
