// Logisim project test2.circ as structural Verilog: 1 circuit, main circuit main
module main (
  input  in_1,
  input  in_2
);

  wire clock_1_out, clock_2_out, nand_1_out, nand_2_out, nor_1_out, nor_2_out;

  Clock clock_1 (.out(clock_1_out));
  Clock clock_2 (.out(clock_2_out));
  nand nand_1 (nand_1_out, in_1, nand_2_out);
  nand nand_2 (nand_2_out, nand_1_out, in_2);
  nor nor_1 (nor_1_out, clock_1_out, nor_2_out);
  nor nor_2 (nor_2_out, nor_1_out, clock_2_out);
endmodule
