// Logisim project test_from_BFHmegaFunction_to_JTAG_UART.circ as structural Verilog: 1 circuit, main circuit main
module main (
);

  // Rv32im #(.SocBusSelection("")) rv32im_1: pin names not known
  // Nios2 #(.SocBusSelection("")) nios2_1: pin names not known
  // SocBus #(.SocBusIdentifier('h000001A0E74C69397b44f854)) socbus_1: pin names not known
  // Socmem #(.SocBusSelection("")) socmem_1: pin names not known
  // SocPio #(.SocBusSelection("")) socpio_1: pin names not known
  // SocVga #(.SocBusSelection("")) socvga_1: pin names not known
  // SocJtagUart #(.SocBusSelection("")) socjtaguart_1: pin names not known
  // TclConsoleReds tclconsolereds_1: pin names not known
  // PlaRom plarom_1: pin names not known
  // TclGeneric #(.content("library ieee;\nuse ieee.std_logic_1164.all;\n\nentity TCL_Generic is\n  port(\n    --Insert input ports below\n    horloge_i  : in  std_logic;                    -- input bit example\n    val_i      : in  std_logic_vector(3 downto 0); -- input vector example\n\n	  --Insert output ports below\n    max_o      : out std_logic;                    -- output bit example\n    cpt_o      : out std_logic_Vector(3 downto 0)  -- output vector example\n  );\nend TCL_Generic;")) tclgeneric_1: pin names not known
  // Digital_Oscilloscope digital_oscilloscope_1: pin names not known
  // Binary_to_BCD_converter binary_to_bcd_converter_1: pin names not known
  // Switch switch_1: pin names not known
  // Buzzer buzzer_1: pin names not known
  Slider slider_1 ();  // open: out
  // BCD_to_7_Segment_decoder bcd_to_7_segment_decoder_1: pin names not known
endmodule
