// Logisim project test_to7442BCD.circ as structural Verilog: 1 circuit, main circuit main
module main (
  input  in_1
);

  wire clock_1_out, n7402_1_pin3, n7402_1_pin4, n7402_1_pin5, n7402_1_pin6, transmission_1_p2;

  Priority_Encoder priority_encoder_1 ();  // open: in0, in1, in2, in3, in4, in5, in6, in7, out, en_in, gs, en_out
  D_Flip_Flop d_ff_1 ();  // open: D, clk, Q, Qn, preset, reset
  // Shift_Register shift_register_1: pin names not known
  ROM rom_1 ();  // open: addr, data
  LED led_1 ();  // open: in
  Hex_Digit_Display hex_digit_display_1 ();  // open: value, dp
  // PortIO portio_1: pin names not known
  _7400 u_7400_1 ();  // open: pin1, pin2, pin3, pin4, pin5, pin6, pin13, pin12, pin11, pin10, pin9, pin8
  _7404 u_7404_1 ();  // open: pin1, pin2, pin3, pin4, pin5, pin6, pin13, pin12, pin11, pin10, pin9, pin8
  _7410 u_7410_1 ();  // open: pin1, pin2, pin3, pin4, pin5, pin6, pin13, pin12, pin11, pin10, pin9, pin8
  _7413 u_7413_1 ();  // open: pin1, pin2, pin3, pin4, pin5, pin6, pin13, pin12, pin11, pin10, pin9, pin8
  _7418 u_7418_1 ();  // open: pin1, pin2, pin3, pin4, pin5, pin6, pin13, pin12, pin11, pin10, pin9, pin8
  _7424 u_7424_1 ();  // open: pin1, pin2, pin3, pin4, pin5, pin6, pin13, pin12, pin11, pin10, pin9, pin8
  _7430 u_7430_1 ();  // open: pin1, pin2, pin3, pin4, pin5, pin6, pin13, pin12, pin11, pin10, pin9, pin8
  _7434 u_7434_1 ();  // open: pin1, pin2, pin3, pin4, pin5, pin6, pin13, pin12, pin11, pin10, pin9, pin8
  // Probe on nothing
  Pull_Resistor pull_resistor_1 ();  // open: node
  Clock clock_1 (.out(clock_1_out));
  BitSelector bitselector_1 ();  // open: in, out, sel
  Subtractor subtractor_1 ();  // open: a, b, out, bin, bout
  FPMultiplier fpmultiplier_1 ();  // open: a, b, out
  FPDivider fpdivider_1 ();  // open: a, b, out
  T_Flip_Flop t_ff_1 ();  // open: T, clk, Q, Qn, reset, preset
  DotMatrix dotmatrix_1 ();  // open: col0, col1, col2, col3, col4
  // ReptarLB reptarlb_1: pin names not known
  _7420 u_7420_1 ();  // open: pin1, pin2, pin3, pin4, pin5, pin6, pin13, pin12, pin11, pin10, pin9, pin8
  // Buffer buffer_1 is placed but not wired
  // NOT_Gate not_1 is placed but not wired
  Adder adder_1 ();  // open: a, b, out, cin, cout
  // FPNegator fpnegator_1: pin names not known
  J_K_Flip_Flop j_k_ff_1 ();  // open: J, K, clk, Q, Qn, preset, reset
  Random random_1 ();  // open: clr, next, clk, out
  RAM ram_1 ();  // open: addr, we, oe, clk, din, dout
  LedBar ledbar_1 ();  // open: led0, led1, led2, led3, led4, led5, led6, led7
  TTY tty_1 ();  // open: data, clk, we, clr
  _7402 u_7402_1 (
    .pin3(n7402_1_pin3), .pin4(n7402_1_pin4), .pin5(n7402_1_pin5), .pin6(n7402_1_pin6));  // open: pin1, pin2, pin13, pin12, pin11, pin10, pin9, pin8
  // OR_Gate or_1 is placed but not wired
  // AND_Gate and_1 is placed but not wired
  Transistor transistor_1 ();  // open: in, out, gate
  // Transmission_Gate transmission_1: pin names not known; wires that end beside it: clock_1_out, transmission_1_p2, in_1, 1'b0, 1'b1, 1'b1
  PLA #(.\table ("")) pla_1 ();  // open: in, out
  POR por_1 ();  // open: out
  Multiplier multiplier_1 ();  // open: a, b, out, cin, cout
  FPSubtractor fpsubtractor_1 ();  // open: a, b, out
  S_R_Flip_Flop s_r_ff_1 ();  // open: S, R, clk, Q, reset, Qn, preset
  // RGB_Video rgb_video_1: pin names not known
  _7408 u_7408_1 (
    .pin13(n7402_1_pin3), .pin12(n7402_1_pin4), .pin11(n7402_1_pin5), .pin10(n7402_1_pin6));  // open: pin1, pin2, pin3, pin4, pin5, pin6, pin9, pin8
  _7411 u_7411_1 ();  // open: pin1, pin2, pin3, pin4, pin5, pin6, pin13, pin12, pin11, pin10, pin9, pin8
  _7414 u_7414_1 ();  // open: pin1, pin2, pin3, pin4, pin5, pin6, pin13, pin12, pin11, pin10, pin9, pin8
  _7419 u_7419_1 ();  // open: pin1, pin2, pin3, pin4, pin5, pin6, pin13, pin12, pin11, pin10, pin9, pin8
  _7421 u_7421_1 ();  // open: pin1, pin2, pin3, pin4, pin5, pin6, pin13, pin12, pin11, pin10, pin9, pin8
  _7427 u_7427_1 ();  // open: pin1, pin2, pin3, pin4, pin5, pin6, pin13, pin12, pin11, pin10, pin9, pin8
  _7432 u_7432_1 ();  // open: pin1, pin2, pin3, pin4, pin5, pin6, pin13, pin12, pin11, pin10, pin9, pin8
  _7436 u_7436_1 ();  // open: pin1, pin2, pin3, pin4, pin5, pin6, pin13, pin12, pin11, pin10, pin9, pin8
  // NoConnect on nothing
  Negator negator_1 ();  // open: in, out
  Decoder decoder_1 ();  // open: out0, out1, sel, en
  Divider divider_1 ();  // open: a, b, out, upper, rem
  FPAdder fpadder_1 ();  // open: a, b, out
  // FPComparator fpcomparator_1: pin names not known
  Register register_1 ();  // open: D, en, clk, Q, clr
  Button button_1 ();  // open: out
  Joystick joystick_1 ();  // open: x, y
  // RGBLED rgbled_1: pin names not known
  // NAND_Gate nand_1 is placed but not wired
  // NOR_Gate nor_1 is placed but not wired
  // XOR_Gate xor_1 is placed but not wired
  Bit_Extender bit_extender_1 ();  // open: in, out
  Controlled_Inverter controlled_inverter_1 ();  // open: in, out, en
  Demultiplexer #(.enable("false")) demultiplexer_1 ();  // open: out0, out1, in, sel
  Comparator comparator_1 ();  // open: a, b, gt, eq, lt
  BitFinder bitfinder_1 ();  // open: in, index, found
  // FPToInt fptoint_1: pin names not known
  DipSwitch dipswitch_1 ();  // open: sw1, sw2, sw3, sw4, sw5, sw6, sw7, sw8
  Keyboard keyboard_1 ();  // open: clk, re, clr, avail, data
  _7_Segment_Display u_7_segment_display_1 ();  // open: g, f, a, b, e, d, c, dp
  // XNOR_Gate xnor_1 is placed but not wired
  // Odd_Parity odd_parity_1 is placed but not wired
  // Even_Parity even_parity_1 is placed but not wired
  Controlled_Buffer controlled_buffer_1 ();  // open: in, out, en
  Multiplexer #(.enable("false")) multiplexer_1 ();  // open: in0, in1, out, sel
  Shifter shifter_1 ();  // open: in, dist, out
  BitAdder bitadder_1 ();  // open: in0, out
  // IntToFP inttofp_1: pin names not known
  Counter counter_1 ();  // open: clr, load, up, count, clk, D, carry, Q
endmodule
